// Logisim project ADDERINHO.circ as structural Verilog: 4 circuits, main circuit halfadder
module halfadder (
  input  A,
  input  B,
  output SUM,
  output CARRY
);

  and and_1 (CARRY, A, B);
  xor xor_1 (SUM, A, B);
endmodule

module MAIN (
  input  b3,
  input  A6,
  input  A7,
  input  A8,
  input  A2,
  input  A4,
  input  A5,
  input  A1,
  input  A3,
  input  b6,
  input  b7,
  input  b8,
  input  B1,
  input  B2,
  input  b4,
  input  b5,
  output s8,
  output S1,
  output s2,
  output s7,
  output s6,
  output s4,
  output s5,
  output s3,
  output FLAG
);

  wire full_1_c_out, full_2_c_out, full_3_c_out, full_4_c_out, full_5_c_out, full_6_c_out, halfadder_1_carry;

  halfadder halfadder_1 (.A(A1), .B(B1), .SUM(S1), .CARRY(halfadder_1_carry));
  full full_1 (.A(A2), .B(B2), .C_in(halfadder_1_carry), .sum(s2), .C_Out(full_1_c_out));
  full full_2 (.A(A3), .B(b3), .C_in(full_1_c_out), .sum(s3), .C_Out(full_2_c_out));
  full full_3 (.A(A4), .B(b4), .C_in(full_2_c_out), .sum(s4), .C_Out(full_3_c_out));
  full full_4 (.A(A5), .B(b5), .C_in(full_3_c_out), .sum(s5), .C_Out(full_4_c_out));
  full full_5 (.A(A6), .B(b6), .C_in(full_4_c_out), .sum(s6), .C_Out(full_5_c_out));
  full full_6 (.A(A7), .B(b7), .C_in(full_5_c_out), .sum(s7), .C_Out(full_6_c_out));
  full full_7 (.A(A8), .B(b8), .C_in(full_6_c_out), .sum(s8), .C_Out(FLAG));

  // Notes on the sheet:
  //   A'S
  //   B
  //   B
  //   b's
  //   B
  //   B
  //   B
  //   B
  //   Flag
endmodule

module full (
  input  A,
  input  B,
  input  C_in,
  output sum,
  output C_Out
);

  wire and_1_out, and_2_out, xor_1_out;

  xor xor_1 (xor_1_out, A, B);
  and and_1 (and_1_out, C_in, xor_1_out);
  and and_2 (and_2_out, B, A);
  xor xor_2 (sum, xor_1_out, C_in);
  or or_1 (C_Out, and_1_out, and_2_out);
endmodule

module MAIN2 (
  input  in_1,
  input  in_2,
  input  in_3,
  input  in_4,
  input  in_5,
  input  in_6,
  input  in_7,
  input  in_8,
  input  in_9,
  input  in_10,
  input  in_11,
  input  in_12,
  input  in_13,
  input  in_14,
  input  in_15,
  input  in_16,
  output out_17,
  output out_18,
  output out_19,
  output out_20,
  output out_21,
  output out_22,
  output out_23,
  output out_24,
  output out_25
);

  MAIN main_1 (
    .b3(in_1), .A6(in_2), .A7(in_3), .A8(in_4), .A2(in_5), .A4(in_6), .A5(in_7), .A1(in_8), .A3(in_9),
    .b6(in_10), .b7(in_11), .b8(in_12), .B1(in_13), .B2(in_14), .b4(in_15), .b5(in_16), .s8(out_17),
    .S1(out_18), .s2(out_19), .s7(out_20), .s6(out_21), .s4(out_22), .s5(out_23), .s3(out_24), .FLAG(out_25));
endmodule
